// Logisim project micro.circ as structural Verilog: 1 circuit, main circuit EV20_Superescalar
module EV20_Superescalar (
  input  in_1
);

  wire ALU_is_done, ALU_is_free, ALU_Pipeline_p17, ALUALULAU_cyout, and_1_out, and_2_out, and_3_out,
       and_4_out, and_5_out, bloque1_1_preload, CLK, CLK2, CLK3, CLK4, CYin, dipswitch_1_sw1, HOLD,
       instruction2register_1_p2, LoadStore_p17, MEM_is_done, mem_is_free, not_1_out, not_2_out, not_3_out,
       not_4_out, or_1_out, or_2_out, or_3_out, pipeline_register_2_p7,
       pipeline_register_viewer_1_a_is_enabled, pipeline_register_viewer_1_b_is_enabled,
       pipeline_register_viewer_1_c_is_enabled, pipeline_register_viewer_2_a_is_enabled,
       pipeline_register_viewer_2_b_is_enabled, pipeline_register_viewer_2_c_is_enabled,
       pipeline_register_viewer_3_a_is_enabled, pipeline_register_viewer_3_b_is_enabled,
       pipeline_register_viewer_3_c_is_enabled, pipeline_register_viewer_4_a_is_enabled,
       pipeline_register_viewer_4_b_is_enabled, pipeline_register_viewer_4_c_is_enabled, register_1_q,
       register_2_q, register_bank_viewer_1_a_is_enabled, register_bank_viewer_1_b_is_enabled,
       register_bank_viewer_1_c_is_enabled, uc1_1_p5, uc1_1_p6, UC1_HOLD, undriven, undriven_2, undriven_3,
       undriven_5;
  wire [1:0] MREtapa2Pipeline, MRMW, pipeline_register_1_p13, pipeline_register_1_p15, undriven_4;
  wire [3:0] pipeline_register_1_p12, pipeline_register_viewer_1_a_lsn, pipeline_register_viewer_1_a_msn,
       pipeline_register_viewer_1_b0, pipeline_register_viewer_1_b1, pipeline_register_viewer_1_b2,
       pipeline_register_viewer_1_b3, pipeline_register_viewer_1_b4, pipeline_register_viewer_1_b5,
       pipeline_register_viewer_1_b6, pipeline_register_viewer_1_b7, pipeline_register_viewer_1_b8,
       pipeline_register_viewer_1_b9, pipeline_register_viewer_1_b10, pipeline_register_viewer_1_b11,
       pipeline_register_viewer_1_b12, pipeline_register_viewer_1_b13, pipeline_register_viewer_1_b14,
       pipeline_register_viewer_1_b15, pipeline_register_viewer_1_b16, pipeline_register_viewer_1_b_lsn,
       pipeline_register_viewer_1_b_msn, pipeline_register_viewer_1_c_lsn, pipeline_register_viewer_1_c_msn,
       pipeline_register_viewer_2_a_lsn, pipeline_register_viewer_2_a_msn, pipeline_register_viewer_2_b0,
       pipeline_register_viewer_2_b1, pipeline_register_viewer_2_b2, pipeline_register_viewer_2_b3,
       pipeline_register_viewer_2_b4, pipeline_register_viewer_2_b5, pipeline_register_viewer_2_b6,
       pipeline_register_viewer_2_b7, pipeline_register_viewer_2_b8, pipeline_register_viewer_2_b9,
       pipeline_register_viewer_2_b10, pipeline_register_viewer_2_b11, pipeline_register_viewer_2_b12,
       pipeline_register_viewer_2_b13, pipeline_register_viewer_2_b14, pipeline_register_viewer_2_b15,
       pipeline_register_viewer_2_b16, pipeline_register_viewer_2_b_lsn, pipeline_register_viewer_2_b_msn,
       pipeline_register_viewer_2_c_lsn, pipeline_register_viewer_2_c_msn, pipeline_register_viewer_3_a_lsn,
       pipeline_register_viewer_3_a_msn, pipeline_register_viewer_3_b0, pipeline_register_viewer_3_b1,
       pipeline_register_viewer_3_b2, pipeline_register_viewer_3_b3, pipeline_register_viewer_3_b4,
       pipeline_register_viewer_3_b5, pipeline_register_viewer_3_b6, pipeline_register_viewer_3_b7,
       pipeline_register_viewer_3_b8, pipeline_register_viewer_3_b9, pipeline_register_viewer_3_b10,
       pipeline_register_viewer_3_b11, pipeline_register_viewer_3_b12, pipeline_register_viewer_3_b13,
       pipeline_register_viewer_3_b14, pipeline_register_viewer_3_b15, pipeline_register_viewer_3_b16,
       pipeline_register_viewer_3_b_lsn, pipeline_register_viewer_3_b_msn, pipeline_register_viewer_3_c_lsn,
       pipeline_register_viewer_3_c_msn, pipeline_register_viewer_4_a_lsn, pipeline_register_viewer_4_a_msn,
       pipeline_register_viewer_4_b0, pipeline_register_viewer_4_b1, pipeline_register_viewer_4_b2,
       pipeline_register_viewer_4_b3, pipeline_register_viewer_4_b4, pipeline_register_viewer_4_b5,
       pipeline_register_viewer_4_b6, pipeline_register_viewer_4_b7, pipeline_register_viewer_4_b8,
       pipeline_register_viewer_4_b9, pipeline_register_viewer_4_b10, pipeline_register_viewer_4_b11,
       pipeline_register_viewer_4_b12, pipeline_register_viewer_4_b13, pipeline_register_viewer_4_b14,
       pipeline_register_viewer_4_b15, pipeline_register_viewer_4_b16, pipeline_register_viewer_4_b_lsn,
       pipeline_register_viewer_4_b_msn, pipeline_register_viewer_4_c_lsn, pipeline_register_viewer_4_c_msn,
       register_bank_viewer_1_a_address_n0, register_bank_viewer_1_a_address_n1,
       register_bank_viewer_1_a_address_n2, register_bank_viewer_1_a_address_n3,
       register_bank_viewer_1_a_data_lsn, register_bank_viewer_1_a_data_msn,
       register_bank_viewer_1_b_address_n0, register_bank_viewer_1_b_address_n1,
       register_bank_viewer_1_b_address_n2, register_bank_viewer_1_b_address_n3,
       register_bank_viewer_1_b_data_lsn, register_bank_viewer_1_b_data_msn,
       register_bank_viewer_1_c_address_n0, register_bank_viewer_1_c_address_n1,
       register_bank_viewer_1_c_address_n2, register_bank_viewer_1_c_address_n3,
       register_bank_viewer_1_c_data_lsn, register_bank_viewer_1_c_data_msn;
  wire [5:0] A_Etapa1, ALU_Pipeline_p18, ALU_Pipeline_p19, ALU_Pipeline_p20, B_Etapa1, C_Etapa1, C_Etapa2Alu,
       C_Etapa3, judge_1_a_bus, judge_1_b_bus, LoadStore_p18, LoadStore_p19, LoadStore_p20,
       pipeline_register_1_p16, pipeline_register_1_p18, pipeline_register_1_p19, pipeline_register_2_p16,
       pipeline_register_2_p17, reg_C_address;
  wire [8:8] pipeline_register_1_p14;
  wire [9:0] pipeline_register_1_p17, register_3_q;
  wire [10:0] ProgramCounterReg_pc;
  wire [14:0] ALU_Pipeline_p16, judge_1_reg_out, LoadStore_p16, MicroInstructionROM_microinstruction,
       pipeline_register_2_p15;
  wire [15:0] ALU_RESULT, ALUALULAU_z, BusA_ALU_q, BusA_LS_q, BusB_ALU_q, Constant_K_q, data_1_datamemout,
       instruction2register_1_p6, multiplexer_1_out, reg_A_read, reg_B_read, reg_C_write, register_6_q;
  wire [23:0] BBUS, ProgramMemory_data;

  DipSwitch #(.number(2)) dipswitch_1 (.sw1(dipswitch_1_sw1));  // open: sw2
  // Probe on ProgramCounterReg_pc
  ROM #(.addrWidth(11), .dataWidth(24)) ProgramMemory (.addr(ProgramCounterReg_pc), .data(ProgramMemory_data));
  // Probe on undriven
  // Probe on undriven_2
  // Probe on undriven_3
  // Probe on undriven_4[1]
  // Probe on undriven_4[0]
  // Probe on undriven_5
  and and_1 (and_1_out, BBUS[22], bloque1_1_preload);
  Bloque1 bloque1_1 (.jump_type(BBUS[21:20]), .register_to_test(16'hfff), .CY(CYin), .Preload(bloque1_1_preload));
  or or_1 (or_1_out, HOLD, UC1_HOLD);
  ClockGenerator clocks (.Auto(dipswitch_1_sw1), .ManualCLK(in_1), .CLK(CLK), .CLK2(CLK2), .CLK3(CLK3), .CLK4(CLK4));
  not not_1 (not_1_out, or_2_out);
  Register #(.width(24)) InstructionRegister (
    .D(ProgramMemory_data), .en(not_1_out), .clk(CLK), .Q(BBUS));  // open: clr
  or or_2 (or_2_out, HOLD, UC1_HOLD);
  PCreg ProgramCounterReg (
    .PC(ProgramCounterReg_pc), .HOLD(or_1_out), .Preload(and_1_out), .CLK1(CLK),
    .displacement_or_address(BBUS[15:5]));
  // Probe on BBUS
  Hex_Digit_Display hex_digit_display_1 (.value(register_bank_viewer_1_c_data_msn));  // open: dp
  Hex_Digit_Display hex_digit_display_2 (.value(register_bank_viewer_1_c_data_lsn));  // open: dp
  LED led_1 (.in(register_bank_viewer_1_c_is_enabled));
  Hex_Digit_Display hex_digit_display_3 (.value(register_bank_viewer_1_c_address_n3));  // open: dp
  Hex_Digit_Display hex_digit_display_4 (.value(register_bank_viewer_1_c_address_n2));  // open: dp
  Hex_Digit_Display hex_digit_display_5 (.value(register_bank_viewer_1_c_address_n1));  // open: dp
  Hex_Digit_Display hex_digit_display_6 (.value(register_bank_viewer_1_c_address_n0));  // open: dp
  Hex_Digit_Display hex_digit_display_7 (.value(register_bank_viewer_1_a_data_msn));  // open: dp
  Hex_Digit_Display hex_digit_display_8 (.value(register_bank_viewer_1_a_data_lsn));  // open: dp
  // instruction2register instruction2register_1: pin names not known; wires that end beside it: BBUS, instruction2register_1_p2, A_Etapa1, B_Etapa1, C_Etapa1, instruction2register_1_p6
  or or_3 (or_3_out, HOLD, UC1_HOLD);
  Hex_Digit_Display hex_digit_display_9 (.value(register_bank_viewer_1_a_address_n3));  // open: dp
  Hex_Digit_Display hex_digit_display_10 (.value(register_bank_viewer_1_a_address_n2));  // open: dp
  Micro_Instruction_ROM MicroInstructionROM (
    .Instruction(BBUS), .MicroInstruction(MicroInstructionROM_microinstruction));
  LED led_2 (.in(register_bank_viewer_1_a_is_enabled));
  register_bank_viewer register_bank_viewer_1 (
    .A_is_enabled(register_bank_viewer_1_a_is_enabled), .A_address_N2(register_bank_viewer_1_a_address_n2),
    .B_is_enabled(register_bank_viewer_1_b_is_enabled), .A_address_N1(register_bank_viewer_1_a_address_n1),
    .B_address_N3(register_bank_viewer_1_b_address_n3), .A_data_MSN(register_bank_viewer_1_a_data_msn),
    .A_address_N3(register_bank_viewer_1_a_address_n3), .A_data_out(pipeline_register_1_p18),
    .A_address_N0(register_bank_viewer_1_a_address_n0), .B_address(reg_B_read),
    .B_data_LSN(register_bank_viewer_1_b_data_lsn), .B_data_out(pipeline_register_1_p19),
    .C_is_enabled(register_bank_viewer_1_c_is_enabled), .B_address_N2(register_bank_viewer_1_b_address_n2),
    .B_address_N0(register_bank_viewer_1_b_address_n0), .C_data_LSN(register_bank_viewer_1_c_data_lsn),
    .B_data_MSN(register_bank_viewer_1_b_data_msn), .B_address_N1(register_bank_viewer_1_b_address_n1),
    .C_address(reg_C_write), .C_address_N1(register_bank_viewer_1_c_address_n1),
    .C_address_N0(register_bank_viewer_1_c_address_n0), .C_address_N2(register_bank_viewer_1_c_address_n2),
    .A_address(reg_A_read), .C_address_N3(register_bank_viewer_1_c_address_n3), .C_data_out(reg_C_address),
    .C_data_MSN(register_bank_viewer_1_c_data_msn), .A_data_LSN(register_bank_viewer_1_a_data_lsn));
  Hex_Digit_Display hex_digit_display_11 (.value(register_bank_viewer_1_a_address_n0));  // open: dp
  Hex_Digit_Display hex_digit_display_12 (.value(register_bank_viewer_1_a_address_n1));  // open: dp
  DotMatrix #(.matrixcols(17), .matrixrows(4)) dotmatrix_1 (
    .col0(pipeline_register_viewer_1_b16), .col1(pipeline_register_viewer_1_b15),
    .col2(pipeline_register_viewer_1_b14), .col3(pipeline_register_viewer_1_b13),
    .col4(pipeline_register_viewer_1_b12), .col5(pipeline_register_viewer_1_b11),
    .col6(pipeline_register_viewer_1_b10), .col7(pipeline_register_viewer_1_b9),
    .col8(pipeline_register_viewer_1_b8), .col9(pipeline_register_viewer_1_b7),
    .col10(pipeline_register_viewer_1_b6), .col11(pipeline_register_viewer_1_b5),
    .col12(pipeline_register_viewer_1_b4), .col13(pipeline_register_viewer_1_b3),
    .col14(pipeline_register_viewer_1_b2), .col15(pipeline_register_viewer_1_b1),
    .col16(pipeline_register_viewer_1_b0));
  pipeline_register_viewer pipeline_register_viewer_1 (
    .b16(pipeline_register_viewer_1_b16), .C_in(C_Etapa2Alu), .b1(pipeline_register_viewer_1_b1),
    .A_in(pipeline_register_1_p18), .b6(pipeline_register_viewer_1_b6), .b0(pipeline_register_viewer_1_b0),
    .B_in(pipeline_register_1_p19), .b15(pipeline_register_viewer_1_b15), .b3(pipeline_register_viewer_1_b3),
    .A_is_enabled(pipeline_register_viewer_1_a_is_enabled), .b12(pipeline_register_viewer_1_b12),
    .b2(pipeline_register_viewer_1_b2),
    .microinstruction({pipeline_register_1_p12, pipeline_register_1_p13, pipeline_register_1_p14[8], pipeline_register_1_p15, pipeline_register_1_p16}),
    .b13(pipeline_register_viewer_1_b13), .b5(pipeline_register_viewer_1_b5),
    .A_MSN(pipeline_register_viewer_1_a_msn), .b10(pipeline_register_viewer_1_b10),
    .b4(pipeline_register_viewer_1_b4), .B_MSN(pipeline_register_viewer_1_b_msn),
    .b11(pipeline_register_viewer_1_b11), .b7(pipeline_register_viewer_1_b7),
    .A_LSN(pipeline_register_viewer_1_a_lsn), .b8(pipeline_register_viewer_1_b8),
    .b14(pipeline_register_viewer_1_b14), .B_is_enabled(pipeline_register_viewer_1_b_is_enabled),
    .b9(pipeline_register_viewer_1_b9), .B_LSN(pipeline_register_viewer_1_b_lsn),
    .C_is_enabled(pipeline_register_viewer_1_c_is_enabled), .C_MSN(pipeline_register_viewer_1_c_msn),
    .C_LSN(pipeline_register_viewer_1_c_lsn));
  // Probe on MicroInstructionROM_microinstruction[14:11]
  // Probe on MicroInstructionROM_microinstruction[10:9]
  // Probe on MicroInstructionROM_microinstruction[8]
  // Probe on MicroInstructionROM_microinstruction[7]
  // Probe on MicroInstructionROM_microinstruction[6]
  // Probe on MicroInstructionROM_microinstruction[5:0]
  Hex_Digit_Display hex_digit_display_13 (.value(register_bank_viewer_1_b_data_lsn));  // open: dp
  Hex_Digit_Display hex_digit_display_14 (.value(register_bank_viewer_1_b_data_msn));  // open: dp
  Hex_Digit_Display hex_digit_display_15 (.value(register_bank_viewer_1_b_address_n3));  // open: dp
  Hex_Digit_Display hex_digit_display_16 (.value(register_bank_viewer_1_b_address_n2));  // open: dp
  Hex_Digit_Display hex_digit_display_17 (.value(pipeline_register_viewer_1_c_msn));  // open: dp
  LED led_3 (.in(register_bank_viewer_1_b_is_enabled));
  Hex_Digit_Display hex_digit_display_18 (.value(register_bank_viewer_1_b_address_n0));  // open: dp
  Hex_Digit_Display hex_digit_display_19 (.value(register_bank_viewer_1_b_address_n1));  // open: dp
  LED led_4 (.in(pipeline_register_viewer_1_c_is_enabled));
  Hex_Digit_Display hex_digit_display_20 (.value(pipeline_register_viewer_1_c_lsn));  // open: dp
  // Pipeline_register pipeline_register_1: pin names not known; wires that end beside it: MicroInstructionROM_microinstruction[14:11], MicroInstructionROM_microinstruction[10:9], MicroInstructionROM_microinstruction[8], MicroInstructionROM_microinstruction[7:6], MicroInstructionROM_microinstruction[5:0], instruction2register_1_p2, A_Etapa1, B_Etapa1, C_Etapa1, or_3_out, CLK2, pipeline_register_1_p12, pipeline_register_1_p13, pipeline_register_1_p14[8], pipeline_register_1_p15, pipeline_register_1_p16, pipeline_register_1_p17, pipeline_register_1_p18, pipeline_register_1_p19, C_Etapa2Alu
  LED led_5 (.in(pipeline_register_viewer_1_a_is_enabled));
  Hex_Digit_Display hex_digit_display_21 (.value(pipeline_register_viewer_1_a_lsn));  // open: dp
  Hex_Digit_Display hex_digit_display_22 (.value(pipeline_register_viewer_1_a_msn));  // open: dp
  LED led_6 (.in(pipeline_register_viewer_1_b_is_enabled));
  Hex_Digit_Display hex_digit_display_23 (.value(pipeline_register_viewer_1_b_lsn));  // open: dp
  Hex_Digit_Display hex_digit_display_24 (.value(pipeline_register_viewer_1_b_msn));  // open: dp
  register_bank register_bank_1 (
    .register_in_address(reg_C_address), .register_in_data(reg_C_write), .clk(CLK),
    .register_out_A_data(reg_A_read), .register_out_B_data(reg_B_read),
    .register_out_B_address(pipeline_register_1_p19), .register_out_A_address(pipeline_register_1_p18));  // open: register_out_aux_address, register_out_aux_data
  // UC1 uc1_1: pin names not known; wires that end beside it: HOLD, pipeline_register_1_p15, ALU_is_free, mem_is_free, uc1_1_p5, uc1_1_p6, UC1_HOLD
  Register #(.width(1)) register_1 (.D(uc1_1_p5), .clk(CLK2), .Q(register_1_q));  // open: en, clr
  Register #(.width(16), .trigger("falling")) Constant_K (
    .D(instruction2register_1_p6), .clk(CLK2), .Q(Constant_K_q));  // open: en, clr
  Register #(.width(1), .trigger("falling")) register_2 (.D(uc1_1_p6), .clk(CLK2), .Q(register_2_q));  // open: en, clr
  not not_2 (not_2_out, pipeline_register_1_p14[8]);
  Register #(.width(16)) BusA_ALU (.D(multiplexer_1_out), .en(uc1_1_p5), .clk(CLK2), .Q(BusA_ALU_q));  // open: clr
  Multiplexer #(.width(16), .enable("false")) multiplexer_1 (
    .in0(Constant_K_q), .in1(reg_A_read), .out(multiplexer_1_out), .sel(not_2_out));
  Register #(.width(16)) BusB_ALU (.D(reg_B_read), .en(uc1_1_p5), .clk(CLK2), .Q(BusB_ALU_q));  // open: clr
  Register #(.width(10)) register_3 (
    .D(pipeline_register_1_p17), .en(uc1_1_p6), .clk(CLK2), .Q(register_3_q));  // open: clr
  DotMatrix #(.matrixcols(17), .matrixrows(4)) dotmatrix_2 (
    .col0(pipeline_register_viewer_2_b16), .col1(pipeline_register_viewer_2_b15),
    .col2(pipeline_register_viewer_2_b14), .col3(pipeline_register_viewer_2_b13),
    .col4(pipeline_register_viewer_2_b12), .col5(pipeline_register_viewer_2_b11),
    .col6(pipeline_register_viewer_2_b10), .col7(pipeline_register_viewer_2_b9),
    .col8(pipeline_register_viewer_2_b8), .col9(pipeline_register_viewer_2_b7),
    .col10(pipeline_register_viewer_2_b6), .col11(pipeline_register_viewer_2_b5),
    .col12(pipeline_register_viewer_2_b4), .col13(pipeline_register_viewer_2_b3),
    .col14(pipeline_register_viewer_2_b2), .col15(pipeline_register_viewer_2_b1),
    .col16(pipeline_register_viewer_2_b0));
  pipeline_register_viewer pipeline_register_viewer_2 (
    .b16(pipeline_register_viewer_2_b16), .C_in(ALU_Pipeline_p20), .b1(pipeline_register_viewer_2_b1),
    .A_in(ALU_Pipeline_p18), .b6(pipeline_register_viewer_2_b6), .b0(pipeline_register_viewer_2_b0),
    .B_in(ALU_Pipeline_p19), .b15(pipeline_register_viewer_2_b15), .b3(pipeline_register_viewer_2_b3),
    .A_is_enabled(pipeline_register_viewer_2_a_is_enabled), .b12(pipeline_register_viewer_2_b12),
    .b2(pipeline_register_viewer_2_b2),
    .microinstruction({ALU_Pipeline_p16[14:8], MREtapa2Pipeline, ALU_Pipeline_p16[5:0]}),
    .b13(pipeline_register_viewer_2_b13), .b5(pipeline_register_viewer_2_b5),
    .A_MSN(pipeline_register_viewer_2_a_msn), .b10(pipeline_register_viewer_2_b10),
    .b4(pipeline_register_viewer_2_b4), .B_MSN(pipeline_register_viewer_2_b_msn),
    .b11(pipeline_register_viewer_2_b11), .b7(pipeline_register_viewer_2_b7),
    .A_LSN(pipeline_register_viewer_2_a_lsn), .b8(pipeline_register_viewer_2_b8),
    .b14(pipeline_register_viewer_2_b14), .B_is_enabled(pipeline_register_viewer_2_b_is_enabled),
    .b9(pipeline_register_viewer_2_b9), .B_LSN(pipeline_register_viewer_2_b_lsn),
    .C_is_enabled(pipeline_register_viewer_2_c_is_enabled), .C_MSN(pipeline_register_viewer_2_c_msn),
    .C_LSN(pipeline_register_viewer_2_c_lsn));
  not not_3 (not_3_out, uc1_1_p5);
  and and_2 (and_2_out, register_1_q, CLK3);
  and and_3 (and_3_out, ~CLK3, register_2_q);  // AND_Gate
  Register #(.width(16)) BusA_LS (.D(reg_A_read), .en(uc1_1_p6), .clk(CLK2), .Q(BusA_LS_q));  // open: clr
  // Probe on BusA_ALU_q
  // Probe on BusB_ALU_q
  DotMatrix #(.matrixcols(17), .matrixrows(4)) dotmatrix_3 (
    .col0(pipeline_register_viewer_3_b16), .col1(pipeline_register_viewer_3_b15),
    .col2(pipeline_register_viewer_3_b14), .col3(pipeline_register_viewer_3_b13),
    .col4(pipeline_register_viewer_3_b12), .col5(pipeline_register_viewer_3_b11),
    .col6(pipeline_register_viewer_3_b10), .col7(pipeline_register_viewer_3_b9),
    .col8(pipeline_register_viewer_3_b8), .col9(pipeline_register_viewer_3_b7),
    .col10(pipeline_register_viewer_3_b6), .col11(pipeline_register_viewer_3_b5),
    .col12(pipeline_register_viewer_3_b4), .col13(pipeline_register_viewer_3_b3),
    .col14(pipeline_register_viewer_3_b2), .col15(pipeline_register_viewer_3_b1),
    .col16(pipeline_register_viewer_3_b0));
  pipeline_register_viewer pipeline_register_viewer_3 (
    .b16(pipeline_register_viewer_3_b16), .C_in(LoadStore_p20), .b1(pipeline_register_viewer_3_b1),
    .A_in(LoadStore_p18), .b6(pipeline_register_viewer_3_b6), .b0(pipeline_register_viewer_3_b0),
    .B_in(LoadStore_p19), .b15(pipeline_register_viewer_3_b15), .b3(pipeline_register_viewer_3_b3),
    .A_is_enabled(pipeline_register_viewer_3_a_is_enabled), .b12(pipeline_register_viewer_3_b12),
    .b2(pipeline_register_viewer_3_b2), .microinstruction({LoadStore_p16[14:8], MRMW, LoadStore_p16[5:0]}),
    .b13(pipeline_register_viewer_3_b13), .b5(pipeline_register_viewer_3_b5),
    .A_MSN(pipeline_register_viewer_3_a_msn), .b10(pipeline_register_viewer_3_b10),
    .b4(pipeline_register_viewer_3_b4), .B_MSN(pipeline_register_viewer_3_b_msn),
    .b11(pipeline_register_viewer_3_b11), .b7(pipeline_register_viewer_3_b7),
    .A_LSN(pipeline_register_viewer_3_a_lsn), .b8(pipeline_register_viewer_3_b8),
    .b14(pipeline_register_viewer_3_b14), .B_is_enabled(pipeline_register_viewer_3_b_is_enabled),
    .b9(pipeline_register_viewer_3_b9), .B_LSN(pipeline_register_viewer_3_b_lsn),
    .C_is_enabled(pipeline_register_viewer_3_c_is_enabled), .C_MSN(pipeline_register_viewer_3_c_msn),
    .C_LSN(pipeline_register_viewer_3_c_lsn));
  not not_4 (not_4_out, uc1_1_p6);
  and and_4 (and_4_out, ALU_is_done, ~ALU_is_free);  // AND_Gate
  Register #(.width(1)) register_4 (.D(ALUALULAU_cyout), .en(1'b1), .clk(CLK2), .Q(CYin));  // open: clr
  LED led_7 (.in(pipeline_register_viewer_2_c_is_enabled));
  Hex_Digit_Display hex_digit_display_25 (.value(pipeline_register_viewer_2_c_msn));  // open: dp
  ALU ALUALULAU (
    .ALUC(ALU_Pipeline_p16[14:11]), .A(BusA_ALU_q), .B(BusB_ALU_q), .CYin(CYin), .Z(ALUALULAU_z),
    .CYout(ALUALULAU_cyout));
  LED led_8 (.in(pipeline_register_viewer_2_a_is_enabled));
  Hex_Digit_Display hex_digit_display_26 (.value(pipeline_register_viewer_2_c_lsn));  // open: dp
  Hex_Digit_Display hex_digit_display_27 (.value(pipeline_register_viewer_2_a_msn));  // open: dp
  // Pipeline_register ALU_Pipeline: pin names not known; wires that end beside it: pipeline_register_1_p12, pipeline_register_1_p13, pipeline_register_1_p14[8], pipeline_register_1_p15, pipeline_register_1_p16, pipeline_register_1_p17, pipeline_register_1_p18, pipeline_register_1_p19, C_Etapa2Alu, not_3_out, CLK3, ALU_Pipeline_p16[14:11], ALU_Pipeline_p16[10:9], ALU_Pipeline_p16[8], MREtapa2Pipeline, ALU_Pipeline_p16[5:0], ALU_Pipeline_p17, ALU_Pipeline_p18, ALU_Pipeline_p19, ALU_Pipeline_p20
  ALU_unit_control alu_unit_control_1 (
    .set_free(and_4_out), .set_not_free(and_2_out), .clk(CLK3), .is_free(ALU_is_free), .is_done(ALU_is_done));
  // Probe on ALUALULAU_z
  LED led_9 (.in(pipeline_register_viewer_3_c_is_enabled));
  Hex_Digit_Display hex_digit_display_28 (.value(pipeline_register_viewer_3_c_lsn));  // open: dp
  Hex_Digit_Display hex_digit_display_29 (.value(pipeline_register_viewer_3_c_msn));  // open: dp
  // Pipeline_register LoadStore: pin names not known; wires that end beside it: pipeline_register_1_p12, pipeline_register_1_p13, pipeline_register_1_p14[8], pipeline_register_1_p15, pipeline_register_1_p16, pipeline_register_1_p17, pipeline_register_1_p18, pipeline_register_1_p19, C_Etapa2Alu, not_4_out, CLK3, LoadStore_p16[14:11], LoadStore_p16[10:9], LoadStore_p16[8], MRMW, LoadStore_p16[5:0], LoadStore_p17, LoadStore_p18, LoadStore_p19, LoadStore_p20
  Hex_Digit_Display hex_digit_display_30 (.value(pipeline_register_viewer_2_a_lsn));  // open: dp
  Hex_Digit_Display hex_digit_display_31 (.value(pipeline_register_viewer_2_b_msn));  // open: dp
  Register #(.width(16)) register_5 (.D(ALUALULAU_z), .en(1'b1), .clk(CLK2), .Q(ALU_RESULT));  // open: clr
  LED led_10 (.in(pipeline_register_viewer_3_a_is_enabled));
  Hex_Digit_Display hex_digit_display_32 (.value(pipeline_register_viewer_3_a_msn));  // open: dp
  Hex_Digit_Display hex_digit_display_33 (.value(pipeline_register_viewer_3_a_lsn));  // open: dp
  and and_5 (and_5_out, MEM_is_done, ~mem_is_free);  // AND_Gate
  Data data_1 (
    .DAddress(register_3_q), .M(MRMW), .clk(CLK2), .Enable(register_2_q), .DataMemInput(BusA_LS_q),
    .DataMemOut(data_1_datamemout));
  LED led_11 (.in(pipeline_register_viewer_2_b_is_enabled));
  Hex_Digit_Display hex_digit_display_34 (.value(pipeline_register_viewer_2_b_lsn));  // open: dp
  LED led_12 (.in(pipeline_register_viewer_3_b_is_enabled));
  Hex_Digit_Display hex_digit_display_35 (.value(pipeline_register_viewer_3_b_msn));  // open: dp
  // Probe on MRMW
  // Probe on LoadStore_p17
  // Probe on data_1_datamemout
  Hex_Digit_Display hex_digit_display_36 (.value(pipeline_register_viewer_3_b_lsn));  // open: dp
  memory_unit_control memory_unit_control_1 (
    .set_free(and_5_out), .set_not_free(and_3_out), .clk(CLK2), .is_free(mem_is_free), .is_done(MEM_is_done));
  // Probe on mem_is_free
  Register #(.width(16)) register_6 (.D(data_1_datamemout), .en(1'b1), .clk(CLK2), .Q(register_6_q));  // open: clr
  Multiplexer #(.width(16), .enable("false")) multiplexer_2 (
    .in0(ALU_RESULT), .in1(register_6_q), .out(reg_C_write), .sel(MEM_is_done));
  judge judge_1 (
    .reg_in_alu({ALU_Pipeline_p16[14:8], MREtapa2Pipeline, ALU_Pipeline_p16[5:0]}),
    .reg_in_memory({LoadStore_p16[14:8], MRMW, LoadStore_p16[5:0]}), .A_alu(ALU_Pipeline_p18),
    .A_mem(LoadStore_p18), .B_alu(ALU_Pipeline_p19), .B_mem(LoadStore_p19), .C_alu(ALU_Pipeline_p20),
    .C_mem(LoadStore_p20), .in_9({MEM_is_done, ALU_is_done}), .reg_out(judge_1_reg_out),
    .A_bus(judge_1_a_bus), .B_bus(judge_1_b_bus), .C_bus(C_Etapa3));
  UC2 uc2_1 (
    .A_etapa_1(A_Etapa1), .B_etapa_1(B_Etapa1), .C_etapa_1(C_Etapa1), .C_etapa_2_ALU(C_Etapa2Alu),
    .ALU_is_done(ALU_is_free), .C_etapa_2_MEM(C_Etapa2Alu), .MEM_is_done(mem_is_free), .C_etapa_3(C_Etapa3),
    .clk(CLK), .out_10(HOLD));
  DotMatrix #(.matrixcols(17), .matrixrows(4)) dotmatrix_4 (
    .col0(pipeline_register_viewer_4_b16), .col1(pipeline_register_viewer_4_b15),
    .col2(pipeline_register_viewer_4_b14), .col3(pipeline_register_viewer_4_b13),
    .col4(pipeline_register_viewer_4_b12), .col5(pipeline_register_viewer_4_b11),
    .col6(pipeline_register_viewer_4_b10), .col7(pipeline_register_viewer_4_b9),
    .col8(pipeline_register_viewer_4_b8), .col9(pipeline_register_viewer_4_b7),
    .col10(pipeline_register_viewer_4_b6), .col11(pipeline_register_viewer_4_b5),
    .col12(pipeline_register_viewer_4_b4), .col13(pipeline_register_viewer_4_b3),
    .col14(pipeline_register_viewer_4_b2), .col15(pipeline_register_viewer_4_b1),
    .col16(pipeline_register_viewer_4_b0));
  pipeline_register_viewer pipeline_register_viewer_4 (
    .b16(pipeline_register_viewer_4_b16), .C_in(reg_C_address), .b1(pipeline_register_viewer_4_b1),
    .A_in(pipeline_register_2_p16), .b6(pipeline_register_viewer_4_b6), .b0(pipeline_register_viewer_4_b0),
    .B_in(pipeline_register_2_p17), .b15(pipeline_register_viewer_4_b15), .b3(pipeline_register_viewer_4_b3),
    .A_is_enabled(pipeline_register_viewer_4_a_is_enabled), .b12(pipeline_register_viewer_4_b12),
    .b2(pipeline_register_viewer_4_b2), .microinstruction(pipeline_register_2_p15),
    .b13(pipeline_register_viewer_4_b13), .b5(pipeline_register_viewer_4_b5),
    .A_MSN(pipeline_register_viewer_4_a_msn), .b10(pipeline_register_viewer_4_b10),
    .b4(pipeline_register_viewer_4_b4), .B_MSN(pipeline_register_viewer_4_b_msn),
    .b11(pipeline_register_viewer_4_b11), .b7(pipeline_register_viewer_4_b7),
    .A_LSN(pipeline_register_viewer_4_a_lsn), .b8(pipeline_register_viewer_4_b8),
    .b14(pipeline_register_viewer_4_b14), .B_is_enabled(pipeline_register_viewer_4_b_is_enabled),
    .b9(pipeline_register_viewer_4_b9), .B_LSN(pipeline_register_viewer_4_b_lsn),
    .C_is_enabled(pipeline_register_viewer_4_c_is_enabled), .C_MSN(pipeline_register_viewer_4_c_msn),
    .C_LSN(pipeline_register_viewer_4_c_lsn));
  LED led_13 (.in(pipeline_register_viewer_4_c_is_enabled));
  Hex_Digit_Display hex_digit_display_37 (.value(pipeline_register_viewer_4_c_lsn));  // open: dp
  Hex_Digit_Display hex_digit_display_38 (.value(pipeline_register_viewer_4_c_msn));  // open: dp
  // Pipeline_register pipeline_register_2: pin names not known; wires that end beside it: judge_1_reg_out[14:11], judge_1_reg_out[10:9], judge_1_reg_out[8], judge_1_reg_out[7:6], judge_1_reg_out[5:0], C_Etapa3, pipeline_register_2_p7, CLK3, judge_1_a_bus, judge_1_b_bus, pipeline_register_2_p15[14:11], pipeline_register_2_p15[10:9], pipeline_register_2_p15[8], pipeline_register_2_p15[7:6], pipeline_register_2_p15[5:0], pipeline_register_2_p16, pipeline_register_2_p17, reg_C_address
  LED led_14 (.in(pipeline_register_viewer_4_a_is_enabled));
  Hex_Digit_Display hex_digit_display_39 (.value(pipeline_register_viewer_4_a_msn));  // open: dp
  Hex_Digit_Display hex_digit_display_40 (.value(pipeline_register_viewer_4_a_lsn));  // open: dp
  LED led_15 (.in(pipeline_register_viewer_4_b_is_enabled));
  Hex_Digit_Display hex_digit_display_41 (.value(pipeline_register_viewer_4_b_msn));  // open: dp
  Hex_Digit_Display hex_digit_display_42 (.value(pipeline_register_viewer_4_b_lsn));  // open: dp
  // NOT_Gate not_5 is placed but not wired

  // Other names for the same wires on the sheet: C_Etapa2Mem[5:0] = C_Etapa2Alu; pulseGenManual = in_1

  // Notes on the sheet:
  //   contents of ProgramMemory (hex, n*v repeats v):
  //   300061 3000a2
  //   splitters que encajar con los registros de pipeline
  //   para hacer copy-paste
  //   probes que encajar en los splitters de arriba
  //   INSTRUCTION
  //   REGISTER
  //   Detecto nueva operacion de memoria
  //   El mux es el de los is_done , el menos significativo es el de la ALU que se pone en 1 cuando termino
endmodule
